// Digital circuit CPU.dig as structural Verilog
module CPU (
  input  clk
);

  wire and_1_out, and_2_out, and_3_out, and_4_out, and_5_out, and_6_out, and_7_out, comparator_1_eq,
       comparator_2_eq, comparator_3_eq, comparator_4_eq, comparator_5_eq, comparator_6_eq, comparator_7_eq,
       comparator_8_eq, comparator_10_eq, comparator_11_lt, comparator_12_eq, comparator_14_eq,
       comparator_15_eq, comparator_16_eq, comparator_17_eq, comparator_18_eq, comparator_19_eq,
       comparator_20_eq, comparator_21_eq, comparator_22_eq, comparator_23_eq, comparator_24_eq,
       comparator_25_eq, driver_2_out, driverinvsel_1_out, multiplexer_4_out, multiplexer_12_out, not_1_out,
       not_2_out, or_1_out, or_2_out, or_3_out, or_4_out, or_5_out, or_8_out, pulldown_1_out, str, t_ff_1_nq;
  wire [0:0] or_6_out, or_7_out;
  wire [2:0] sub_1_s;
  wire [3:0] multiplexer_9_out, multiplexer_11_out, rom_1_d, rom_1_d_4, rom_1_d_5;
  wire [7:0] _1Din, add_1_s, add_3_s, driver_4_out, driver_9_out, in, multiplexer_1_out, multiplexer_5_out,
       multiplexer_6_out, multiplexer_7_out, multiplexer_8_out, multiplexer_10_out, multiplexer_13_out,
       multiplexer_15_out, multiplexer_16_out, multiplexer_17_out, out, ramdualaccess_1_d1,
       ramdualaccess_1_d2, ramdualport_1_d, register_1_q, registerfile_1_da, rom_1_d_3, sub_2_s;
  wire [7:3] sub_1_s_2;
  wire [7:4] rom_1_d_2;
  wire [15:0] _1A, add_2_s, ASCII_Lookup_Table_d, counterpreset_1_out, multiplexer_2_out, multiplexer_3_out,
       multiplexer_14_out, pulldown_3_out, pulldown_9_out;
  wire [15:8] keyboard_1_d, ramdualport_1_d_2;

  Keyboard keyboard_1 (.C(out[0]), .en(1'b1), .D({keyboard_1_d, in}));  // open: av
  PullDown pulldown_1 (.out(pulldown_1_out));
  assign pulldown_1_out = 1'b1 ? clk : 1'bz;  // Driver driver_1
  GPU gpu_1 (.C_VGA(pulldown_1_out), .str(str), ._1A(_1A), ._1Din(_1Din));
  ROM #(.AddrBits(8), .isProgramMemory("true"), .Bits(16)) ASCII_Lookup_Table (
    .A(ramdualaccess_1_d1), .sel(1'b1), .D(ASCII_Lookup_Table_d));
  or or_1 (or_1_out, or_3_out, comparator_3_eq);
  T_FF t_ff_1 (.T(comparator_5_eq), .C(comparator_5_eq), .nQ(t_ff_1_nq));  // open: Q
  assign driver_2_out = t_ff_1_nq ? clk : 1'bz;  // Driver driver_2
  PullDown pulldown_2 (.out(driver_2_out));
  PullDown #(.Bits(16)) pulldown_3 (.out(pulldown_3_out));
  assign pulldown_3_out = or_1_out ? {ramdualport_1_d_2, ramdualport_1_d} : 16'bz;  // Driver driver_3
  Multiplexer #(.Bits(8)) multiplexer_1 (
    .sel(comparator_4_eq), .in_0(ramdualaccess_1_d1), .in_1(rom_1_d_3), .out(multiplexer_1_out));
  assign driver_4_out = comparator_6_eq ? multiplexer_1_out : 8'bz;  // Driver driver_4
  PullDown #(.Bits(8)) pulldown_4 (.out(driver_4_out));
  Multiplexer #(.Bits(16)) multiplexer_2 (
    .sel(or_1_out), .in_0({{8{1'b0}}, driver_4_out}), .in_1(pulldown_3_out), .out(multiplexer_2_out));
  and and_1 (and_1_out, comparator_1_eq, not_1_out);
  Comparator #(.Bits(8)) comparator_1 (.a(8'h4), .b({rom_1_d_2, rom_1_d}), .eq(comparator_1_eq));  // open: gt, lt
  Comparator #(.Bits(4)) comparator_2 (.a(4'b0000), .b(rom_1_d_4), .eq(comparator_2_eq));  // open: gt, lt
  or or_2 (or_2_out, comparator_6_eq, or_3_out, driverinvsel_1_out);
  Multiplexer #(.Bits(16)) multiplexer_3 (
    .sel(driverinvsel_1_out), .in_0(multiplexer_2_out), .in_1(ASCII_Lookup_Table_d), .out(multiplexer_3_out));
  not not_1 (not_1_out, comparator_2_eq);
  Comparator #(.Bits(4)) comparator_3 (.a(rom_1_d_5), .b(4'b0010), .eq(comparator_3_eq));  // open: gt, lt
  Comparator #(.Bits(4)) comparator_4 (.a(4'b0001), .b(rom_1_d_5), .eq(comparator_4_eq));  // open: gt, lt
  assign driverinvsel_1_out = ~1'b0 ? comparator_7_eq : 1'bz;  // DriverInvSel driverinvsel_1
  Multiplexer #(.Selector_Bits(4)) multiplexer_4 (
    .sel(rom_1_d), .in_0(1'b1), .in_1(1'b1), .in_2(1'b0), .in_3(1'b0), .in_4(comparator_2_eq), .in_5(1'b0),
    .in_6(1'b0), .in_7(1'b0), .in_8(and_6_out), .in_9(1'b0), .in_10(1'b1), .in_11(1'b0), .in_12(1'b0),
    .in_13(1'b0), .in_14(1'b0), .in_15(1'b0), .out(multiplexer_4_out));
  Comparator #(.Bits(8)) comparator_5 (.a({8{1'b1}}), .b({rom_1_d_2, rom_1_d}), .eq(comparator_5_eq));  // open: gt, lt
  Comparator #(.Bits(8)) comparator_6 (.a({rom_1_d_2, rom_1_d}), .b(8'h2), .eq(comparator_6_eq));  // open: gt, lt
  CounterPreset #(.Bits(16), .isProgramCounter("true")) counterpreset_1 (
    .en(1'b1), .C(driver_2_out), .dir(1'b0), .in(multiplexer_3_out), .ld(or_2_out), .clr(1'b0),
    .out(counterpreset_1_out));  // open: ovf
  Comparator #(.Bits(8)) comparator_7 (.a(8'h7), .b({rom_1_d_2, rom_1_d}), .eq(comparator_7_eq));  // open: gt, lt
  // Probe on counterpreset_1_out
  ROM #(.AddrBits(16), .isProgramMemory("true"), .Bits(24)) rom_1 (
    .A(counterpreset_1_out), .sel(1'b1), .D({rom_1_d_5, rom_1_d_4, rom_1_d_3, rom_1_d_2, rom_1_d}));
  PullDown #(.Bits(24)) pulldown_5 (.out({rom_1_d_5, rom_1_d_4, rom_1_d_3, rom_1_d_2, rom_1_d}));
  Multiplexer #(.Selector_Bits(4), .Bits(8)) multiplexer_5 (
    .sel(rom_1_d), .in_0({8{1'b0}}), .in_1({8{1'b0}}), .in_2({8{1'b0}}), .in_3({8{1'b0}}), .in_4({8{1'b0}}),
    .in_5({8{1'b0}}), .in_6({rom_1_d_5, rom_1_d_4}), .in_7({8{1'b0}}), .in_8({8{1'b0}}), .in_9({8{1'b0}}),
    .in_10({8{1'b0}}), .in_11({rom_1_d_5, rom_1_d_4}), .in_12({rom_1_d_5, rom_1_d_4}),
    .in_13({rom_1_d_5, rom_1_d_4}), .in_14({8{1'b0}}), .in_15({8{1'b0}}), .out(multiplexer_5_out));
  Sub #(.Bits(8)) sub_1 (.a({rom_1_d_2, rom_1_d}), .b(8'h9), .c_i(1'b0), .s({sub_1_s_2, sub_1_s}));  // open: c_o
  // Probe on {rom_1_d_2, rom_1_d}
  Comparator #(.Bits(8)) comparator_8 (.a(8'h3), .b(rom_1_d_3), .eq(comparator_8_eq));  // open: gt, lt
  // Probe on {sub_1_s_2, sub_1_s}
  // Probe on {rom_1_d_5, rom_1_d_4, rom_1_d_3}
  Multiplexer #(.Selector_Bits(4), .Bits(8)) multiplexer_6 (
    .sel(rom_1_d), .in_0({8{1'b0}}), .in_1(rom_1_d_3), .in_2(rom_1_d_3), .in_3({8{1'b0}}), .in_4(rom_1_d_3),
    .in_5({8{1'b0}}), .in_6(rom_1_d_3), .in_7(rom_1_d_3), .in_8(rom_1_d_3), .in_9(rom_1_d_3),
    .in_10({8{1'b0}}), .in_11(rom_1_d_3), .in_12(rom_1_d_3), .in_13(rom_1_d_3), .in_14({8{1'b0}}),
    .in_15({8{1'b0}}), .out(multiplexer_6_out));
  Break #(.Cycles(276447231)) break_1 (.brk(comparator_8_eq));
  Comparator #(.Bits(8)) comparator_9 (.a(8'hb), .b({rom_1_d_2, rom_1_d}));  // open: gt, eq, lt
  Multiplexer #(.Selector_Bits(2), .Bits(8)) multiplexer_7 (
    .sel(sub_1_s[1:0]), .in_0(ramdualaccess_1_d1), .in_1({8{1'b0}}), .in_2(add_1_s), .in_3({8{1'b0}}),
    .out(multiplexer_7_out));
  Multiplexer #(.Selector_Bits(4), .Bits(8)) multiplexer_8 (
    .sel(rom_1_d), .in_0({rom_1_d_5, rom_1_d_4}), .in_1({rom_1_d_5, rom_1_d_4}), .in_2({8{1'b0}}),
    .in_3({8{1'b0}}), .in_4(rom_1_d_3), .in_5({8{1'b0}}), .in_6({8{1'b0}}), .in_7({8{1'b0}}),
    .in_8({8{1'b0}}), .in_9({8{1'b0}}), .in_10(rom_1_d_3), .in_11({8{1'b0}}), .in_12({8{1'b0}}),
    .in_13({8{1'b0}}), .in_14({8{1'b0}}), .in_15({8{1'b0}}), .out(multiplexer_8_out));
  Multiplexer #(.Selector_Bits(3), .Bits(4)) multiplexer_9 (
    .sel(sub_1_s), .in_0(4'b1100), .in_1(4'b0000), .in_2(4'b1010), .in_3(4'b0000), .in_4(4'b0000),
    .in_5(4'b0000), .in_6(4'b0000), .in_7(4'b0000), .out(multiplexer_9_out));
  Multiplexer #(.Selector_Bits(4), .Bits(8)) multiplexer_10 (
    .sel(rom_1_d), .in_0(rom_1_d_3), .in_1(ramdualaccess_1_d1), .in_2({8{1'b0}}), .in_3({8{1'b0}}),
    .in_4(in), .in_5({8{1'b0}}), .in_6({8{1'b0}}), .in_7({8{1'b0}}), .in_8(ramdualport_1_d),
    .in_9({8{1'b0}}), .in_10(registerfile_1_da), .in_11({8{1'b0}}), .in_12({8{1'b0}}), .in_13({8{1'b0}}),
    .in_14({8{1'b0}}), .in_15({8{1'b0}}), .out(multiplexer_10_out));
  // Probe on multiplexer_10_out
  Break #(.Cycles(276447231)) break_2 (.brk(comparator_10_eq));
  Multiplexer #(.Selector_Bits(4), .Bits(4)) multiplexer_11 (
    .sel(rom_1_d), .in_0(4'b0000), .in_1(4'b0000), .in_2(4'b0000), .in_3(4'b0000), .in_4(4'b0000),
    .in_5(4'b0000), .in_6(4'b1100), .in_7(4'b0000), .in_8(4'b0000), .in_9(4'b0000), .in_10(4'b1010),
    .in_11(4'b0000), .in_12(4'b0000), .in_13(4'b0000), .in_14(4'b0000), .in_15(4'b0000),
    .out(multiplexer_11_out));
  Comparator #(.Bits(8)) comparator_10 (.a(8'h3), .b(multiplexer_13_out), .eq(comparator_10_eq));  // open: gt, lt
  Multiplexer #(.Selector_Bits(2)) multiplexer_12 (
    .sel(sub_1_s[1:0]), .in_0(1'b1), .in_1(1'b0), .in_2(1'b1), .in_3(1'b0), .out(multiplexer_12_out));
  RegisterFile #(.AddrBits(4), .Bits(8)) registerfile_1 (
    .Din(multiplexer_7_out), .we(multiplexer_12_out), .Rw(multiplexer_9_out), .C(driver_2_out),
    .Ra(multiplexer_11_out), .Rb(4'b0000), .Da(registerfile_1_da));  // open: Db
  Multiplexer #(.Bits(8)) multiplexer_13 (
    .sel(comparator_11_lt), .in_0(multiplexer_8_out), .in_1(multiplexer_6_out), .out(multiplexer_13_out));
  Comparator #(.Bits(8)) comparator_11 (
    .a(multiplexer_8_out), .b(multiplexer_6_out), .lt(comparator_11_lt));  // open: gt, eq
  Comparator #(.Bits(8)) comparator_12 (.a(8'h6), .b({rom_1_d_2, rom_1_d}), .eq(comparator_12_eq));  // open: gt, lt
  or or_3 (or_3_out, and_3_out, and_2_out);
  RAMDualAccess #(.AddrBits(8), .Bits(8)) ramdualaccess_1 (
    .str(multiplexer_4_out), .C(driver_2_out), .ld(1'b1), .A1(multiplexer_13_out), .Din1(multiplexer_10_out),
    .A2(multiplexer_5_out), .D1(ramdualaccess_1_d1), .D2(ramdualaccess_1_d2));
  Comparator #(.Bits(8)) comparator_13 (.a({rom_1_d_2, rom_1_d}), .b(8'h6), .eq(str));  // open: gt, lt
  and and_2 (and_2_out, comparator_15_eq, comparator_14_eq);
  and and_3 (and_3_out, comparator_16_eq, not_2_out);
  // Probe on ramdualaccess_1_d1
  // Probe on ramdualaccess_1_d2
  Add #(.Bits(8)) add_1 (.a(ramdualaccess_1_d2), .b(ramdualaccess_1_d1), .c_i(1'b0), .s(add_1_s));  // open: c_o
  not not_2 (not_2_out, comparator_14_eq);
  assign out = and_1_out ? ramdualaccess_1_d1 : 8'bz;  // Driver driver_5
  PullDown #(.Bits(8)) pulldown_6 (.out(out));
  Comparator #(.Bits(8)) comparator_14 (
    .a(ramdualaccess_1_d2), .b(ramdualaccess_1_d1), .eq(comparator_14_eq));  // open: gt, lt
  Comparator #(.Bits(8)) comparator_15 (.a({rom_1_d_2, rom_1_d}), .b(8'hc), .eq(comparator_15_eq));  // open: gt, lt
  Comparator #(.Bits(8)) comparator_16 (.a({rom_1_d_2, rom_1_d}), .b(8'hd), .eq(comparator_16_eq));  // open: gt, lt
  assign _1A = str ? {ramdualaccess_1_d1, ramdualaccess_1_d2} : 16'bz;  // Driver driver_6
  PullDown #(.Bits(16)) pulldown_7 (.out(_1A));
  assign _1Din = comparator_12_eq ? registerfile_1_da : 8'bz;  // Driver driver_7
  PullDown #(.Bits(8)) pulldown_8 (.out(_1Din));
  Comparator #(.Bits(8)) comparator_17 (.a(8'hd), .b({rom_1_d_2, rom_1_d}), .eq(comparator_17_eq));  // open: gt, lt
  Comparator #(.Bits(8)) comparator_18 (.a(8'hc), .b({rom_1_d_2, rom_1_d}), .eq(comparator_18_eq));  // open: gt, lt
  Comparator #(.Bits(4)) comparator_19 (.a(rom_1_d_5), .b(4'b0010), .eq(comparator_19_eq));  // open: gt, lt
  Comparator #(.Bits(4)) comparator_20 (.a(4'b0001), .b(rom_1_d_4), .eq(comparator_20_eq));  // open: gt, lt
  Comparator #(.Bits(8)) comparator_21 (.a(8'h2), .b({rom_1_d_2, rom_1_d}), .eq(comparator_21_eq));  // open: gt, lt
  or or_4 (or_4_out, comparator_17_eq, comparator_18_eq);
  and and_4 (and_4_out, comparator_19_eq, comparator_21_eq);
  and and_5 (and_5_out, comparator_20_eq, comparator_21_eq);
  or or_5 (or_5_out, and_5_out, comparator_7_eq);
  or or_6 (or_6_out[0], or_5_out, and_7_out);
  Add #(.Bits(16)) add_2 (.a(16'h1), .b(counterpreset_1_out), .c_i(1'b0), .s(add_2_s));  // open: c_o
  PullDown #(.Bits(16)) pulldown_9 (.out(pulldown_9_out));
  assign pulldown_9_out = or_5_out ? add_2_s : 16'bz;  // Driver driver_8
  Comparator #(.Bits(4)) comparator_22 (.a(4'b0000), .b(rom_1_d_4), .eq(comparator_22_eq));  // open: gt, lt
  Comparator #(.Bits(4)) comparator_23 (.a(4'b0001), .b(rom_1_d_4), .eq(comparator_23_eq));  // open: gt, lt
  Comparator #(.Bits(8)) comparator_24 (.a(8'h8), .b({rom_1_d_2, rom_1_d}), .eq(comparator_24_eq));  // open: gt, lt
  or or_7 (or_7_out[0], and_4_out, or_4_out, and_6_out);
  Multiplexer #(.Bits(16)) multiplexer_14 (
    .sel(and_7_out), .in_0(pulldown_9_out), .in_1({{8{1'b0}}, driver_9_out}), .out(multiplexer_14_out));
  and and_6 (and_6_out, comparator_23_eq, comparator_24_eq);
  and and_7 (and_7_out, comparator_22_eq, comparator_24_eq);
  or or_8 (or_8_out, or_6_out[0], or_7_out[0]);
  assign driver_9_out = and_7_out ? multiplexer_15_out : 8'bz;  // Driver driver_9
  Multiplexer #(.Bits(8)) multiplexer_15 (
    .sel(comparator_25_eq), .in_0(ramdualaccess_1_d1), .in_1(rom_1_d_3), .out(multiplexer_15_out));
  PullDown #(.Bits(8)) pulldown_10 (.out(driver_9_out));
  Register #(.Bits(8)) register_1 (.D(multiplexer_17_out), .C(driver_2_out), .en(or_8_out), .Q(register_1_q));
  Comparator #(.Bits(4)) comparator_25 (.a(rom_1_d_5), .b(4'b0001), .eq(comparator_25_eq));  // open: gt, lt
  Add #(.Bits(8)) add_3 (.a(register_1_q), .b({{7{1'b0}}, or_6_out[0]}), .c_i(1'b0), .s(add_3_s));  // open: c_o
  Sub #(.Bits(8)) sub_2 (.a(register_1_q), .b({{7{1'b0}}, or_7_out[0]}), .c_i(1'b0), .s(sub_2_s));  // open: c_o
  Multiplexer #(.Bits(8)) multiplexer_16 (
    .sel(or_7_out[0]), .in_0(multiplexer_17_out), .in_1(register_1_q), .out(multiplexer_16_out));
  // Probe on register_1_q
  // Probe on multiplexer_14_out
  // Probe on sub_2_s
  Multiplexer #(.Bits(8)) multiplexer_17 (.sel(or_7_out[0]), .in_0(add_3_s), .in_1(sub_2_s), .out(multiplexer_17_out));
  // Probe on multiplexer_16_out
  RAMDualPort #(.AddrBits(8), .isProgramMemory("true"), .Bits(16)) ramdualport_1 (
    .A(multiplexer_16_out), .Din(multiplexer_14_out), .str(or_6_out[0]), .C(driver_2_out), .ld(or_7_out[0]),
    .D({ramdualport_1_d_2, ramdualport_1_d}));
  // Probe on add_3_s

  // Notes on the sheet:
  //   clk: Hz: 25175000
  //   contents of ASCII_Lookup_Table (hex, n*v repeats v):
  //   65*0,18,5b,9e,c9,106,13a,165,199,1d3,204,235,266,28b,2cb,30e,357
  //   ,38b,3da,417,44e,479,4b0,4de,518,540,565
  //   Do data go in?
  //   contents of rom_1 (hex, n*v repeats v):
  //   ff00,9,3,61200,20100,30100,2c0100,2d0000,7a0800,2b04,100908,2d2b0c
  //   ,2b07,12c04,37a0b,30a,100902,ff,2100b,100a,3110b,110a,111006,200002
  //   ,100100,110100,10602,100200,110100,10602,100300,110100,10602,100400
  //   ,110100,10602,100500,110100,10602,100600,110100,10602,100700,110100
  //   ,10602,100000,110200,10602,100400,110200,10602,100000,110300,10602
  //   ,100400,110300,10602,100000,110400,10602,100400,110400,10602,100000
  //   ,110500,10602,100400,110500,10602,100100,110600,10602,100200,110600
  //   ,10602,100300,110600,10602,100400,110600,10602,100500,110600,10602
  //   ,100600,110600,10602,100700,110600,10602,200002,100000,110100
  //   ,10602,100100,110100,10602,100200,110100,10602,100300,110100,10602
  //   ,100400,110100,10602,100500,110100,10602,100600,110100,10602,100700
  //   ,110100,10602,100000,110200,10602,100300,110200,10602,100700,110200
  //   ,10602,100000,110300,10602,100300,110300,10602,100700,110300,10602
  //   ,100000,110400,10602,100300,110400,10602,100700,110400,10602,100100
  //   ,110500,10602,100200,110500,10602,100400,110500,10602,100500,110500
  //   ,10602,100600,110500,10602,200002,100200,110000,10602,100300,110000
  //   ,10602,100400,110000,10602,100500,110000,10602,100100,110100,10602
  //   ,100600,110100,10602,100000,110200,10602,100700,110200,10602,100000
  //   ,110300,10602,100700,110300,10602,100000,110400,10602,100700,110400
  //   ,10602,100000,110500,10602,100700,110500,10602,200002,100000,110100
  //   ,10602,100100,110100,10602,100200,110100,10602,100300,110100,10602
  //   ,100400,110100,10602,100500,110100,10602,100600,110100,10602,100700
  //   ,110100,10602,100000,110200,10602,100700,110200,10602,100000,110300
  //   ,10602,100700,110300,10602,100000,110400,10602,100700,110400,10602
  //   ,100100,110500,10602,100200,110500,10602,100300,110500,10602,100400
  //   ,110500,10602,100500,110500,10602,100600,110500,10602,200002,100000
  //   ,110200,10602,100100,110200,10602,100200,110200,10602,100300,110200
  //   ,10602,100400,110200,10602,100500,110200,10602,100600,110200,10602
  //   ,100700,110200,10602,100000,110300,10602,100300,110300,10602,100700
  //   ,110300,10602,100000,110400,10602,100300,110400,10602,100700,110400
  //   ,10602,100000,110500,10602,100300,110500,10602,100700,110500,10602
  //   ,200002,100000,110200,10602,100100,110200,10602,100200,110200
  //   ,10602,100300,110200,10602,100400,110200,10602,100500,110200,10602
  //   ,100600,110200,10602,100700,110200,10602,100000,110300,10602,100300
  //   ,110300,10602,100000,110400,10602,100300,110400,10602,100000,110500
  //   ,10602,100300,110500,10602,200002,100200,110100,10602,100300,110100
  //   ,10602,100400,110100,10602,100500,110100,10602,100600,110100,10602
  //   ,100100,110200,10602,100700,110200,10602,100100,110300,10602,100500
  //   ,110300,10602,100700,110300,10602,100100,110400,10602,100500,110400
  //   ,10602,100700,110400,10602,100100,110500,10602,100500,110500,10602
  //   ,100700,110500,10602,100600,110600,10602,200002,100000,110100
  //   ,10602,100100,110100,10602,100200,110100,10602,100300,110100,10602
  //   ,100400,110100,10602,100500,110100,10602,100600,110100,10602,100700
  //   ,110100,10602,100300,110200,10602,100300,110300,10602,100300,110400
  //   ,10602,100000,110500,10602,100100,110500,10602,100200,110500,10602
  //   ,100300,110500,10602,100400,110500,10602,100500,110500,10602,100600
  //   ,110500,10602,100700,110500,10602,200002,100000,110100,10602,100700
  //   ,110100,10602,100000,110200,10602,100700,110200,10602,100000,110300
  //   ,10602,100100,110300,10602,100200,110300,10602,100300,110300,10602
  //   ,100400,110300,10602,100500,110300,10602,100600,110300,10602,100700
  //   ,110300,10602,100000,110400,10602,100700,110400,10602,100000,110500
  //   ,10602,100700,110500,10602,200002,100000,110100,10602,100700,110100
  //   ,10602,100000,110200,10602,100700,110200,10602,100000,110300,10602
  //   ,100700,110300,10602,100000,110400,10602,100100,110400,10602,100200
  //   ,110400,10602,100300,110400,10602,100400,110400,10602,100500,110400
  //   ,10602,100600,110400,10602,100700,110400,10602,100000,110500,10602
  //   ,100000,110600,10602,200002,100000,110100,10602,100100,110100
  //   ,10602,100200,110100,10602,100300,110100,10602,100400,110100,10602
  //   ,100500,110100,10602,100600,110100,10602,100700,110100,10602,100300
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  //   Data out address 2
  //   Data in
  //   Data out address 1
  //   In address
  //   Data in address
  //   Out address
  //   Write enable
endmodule
