// Digital circuit GPU.dig as structural Verilog
module GPU (
  input  C_VGA,
  input  str,
  input  [15:0] _1A,
  input  [7:0] _1Din
);

  wire and_1_out, comparator_1_eq, comparator_2_eq, comparator_3_eq, comparator_4_eq, comparator_5_eq,
       comparator_6_eq, comparator_7_lt, comparator_8_lt, rs_ff_as_1_nq, rs_ff_as_2_nq;
  wire [7:0] ramdualaccess_1_d2;
  wire [11:0] counter_1_out, counter_2_out, driver_1_out, driver_2_out;
  wire [11:8] div_1_q_2, div_2_q;
  wire [15:0] div_1_q;

  Counter #(.Bits(12)) counter_1 (.en(1'b1), .C(C_VGA), .clr(comparator_3_eq), .out(counter_1_out));  // open: ovf
  Counter #(.Bits(12)) counter_2 (
    .en(1'b1), .C(comparator_3_eq), .clr(comparator_6_eq), .out(counter_2_out));  // open: ovf
  Comparator #(.Bits(12)) comparator_1 (.a(counter_1_out), .b(12'h290), .eq(comparator_1_eq));  // open: gt, lt
  Comparator #(.Bits(12)) comparator_2 (.a(counter_1_out), .b(12'h2f0), .eq(comparator_2_eq));  // open: gt, lt
  Comparator #(.Bits(12)) comparator_3 (.a(counter_1_out), .b(12'h31f), .eq(comparator_3_eq));  // open: gt, lt
  Comparator #(.Bits(12)) comparator_4 (.a(counter_2_out), .b(12'h1ea), .eq(comparator_4_eq));  // open: gt, lt
  Comparator #(.Bits(12)) comparator_5 (.a(counter_2_out), .b(12'h1ec), .eq(comparator_5_eq));  // open: gt, lt
  Comparator #(.Bits(12)) comparator_6 (.a(counter_2_out), .b(12'h20c), .eq(comparator_6_eq));  // open: gt, lt
  RS_FF_AS rs_ff_as_1 (.S(comparator_1_eq), .R(comparator_2_eq), .nQ(rs_ff_as_1_nq));  // open: Q
  RS_FF_AS rs_ff_as_2 (.S(comparator_4_eq), .R(comparator_5_eq), .nQ(rs_ff_as_2_nq));  // open: Q
  Comparator #(.Bits(12)) comparator_7 (.a(counter_1_out), .b(12'h280), .lt(comparator_7_lt));  // open: gt, eq
  RAMDualAccess #(.AddrBits(16), .Bits(8)) ramdualaccess_1 (
    .str(str), .C(C_VGA), .ld(and_1_out), .A1(_1A), .Din1(_1Din), .A2(div_1_q), .D2(ramdualaccess_1_d2));  // open: D1
  Comparator #(.Bits(12)) comparator_8 (.a(counter_2_out), .b(12'h1e0), .lt(comparator_8_lt));  // open: gt, eq
  and and_1 (and_1_out, comparator_7_lt, comparator_8_lt);
  Div #(.Bits(12)) div_1 (.a(driver_1_out), .b(12'h4), .q({div_1_q_2, div_1_q[7:0]}));  // open: r
  assign driver_1_out = comparator_7_lt ? counter_1_out : 12'bz;  // Driver driver_1
  assign driver_2_out = comparator_8_lt ? counter_2_out : 12'bz;  // Driver driver_2
  Div #(.Bits(12)) div_2 (.a(driver_2_out), .b(12'h4), .q({div_2_q, div_1_q[15:8]}));  // open: r
  VGA vga_1 (
    .R(ramdualaccess_1_d2[1:0]), .G(ramdualaccess_1_d2[3:2]), .B(ramdualaccess_1_d2[5:4]), .H(rs_ff_as_1_nq),
    .V(rs_ff_as_2_nq), .C(C_VGA));

  // Notes on the sheet:
  //   C_VGA: Hz: 2147483647
endmodule
