// Digital circuit MAIN.dig as structural Verilog
module MAIN (
  input  clk
);

  wire comparator_1_eq, not_1_out, pulldown_2_out, undriven, undriven_2;
  wire [7:0] keyboard_1_d, undriven_4, undriven_5;
  wire [15:0] register_1_q, undriven_3;
  wire [15:8] keyboard_1_d_2;

  CPU cpu_1 ();  // open: clk
  not not_1 (not_1_out, comparator_1_eq);
  Keyboard keyboard_1 (.C(undriven_5[0]), .en(1'b1), .D({keyboard_1_d_2, keyboard_1_d}));  // open: av
  // Probe on register_1_q
  Register #(.Bits(16)) register_1 (.D({keyboard_1_d_2, keyboard_1_d}), .C(clk), .en(not_1_out), .Q(register_1_q));
  Comparator #(.Bits(16)) comparator_1 (
    .a({keyboard_1_d_2, keyboard_1_d}), .b({16{1'b0}}), .eq(comparator_1_eq));  // open: gt, lt
  PullDown #(.Bits(16)) pulldown_1 (.out({keyboard_1_d_2, keyboard_1_d}));
  PullDown pulldown_2 (.out(pulldown_2_out));
  assign pulldown_2_out = undriven ? clk : 1'bz;  // Driver driver_1
  // Probe on undriven_5
  // Probe on undriven_2
  // Probe on undriven_3
  GPU gpu_1 (.C_VGA(pulldown_2_out), .str(undriven_2), ._1A(undriven_3), ._1Din(undriven_4));
  // Probe on undriven_4

  // Notes on the sheet:
  //   clk: Hz: 10
endmodule
